# Fritzing sketch TwoMotor (saved by Fritzing 0.9.2b)
breadboards: 1

parts:
  Part1 = Motor Driver 1A Dual TB6612FNG
  Part2 = Arduino Nano (Rev3.0)
  M1 = DC Motor
  M2 = DC Motor
  U1 = LIPO-110mAh [package=lipo-110]
  Part3 = Bluetooth Mate Silver

nets:
  N1: Part1.B01, M1.pin_1
  N2: Part1.B02, M1.pin_2
  N3: Part1.A02, M2.pin_1
  N4: Part1.A01, M2.pin_2
  GND: Part1.GND, Part2.GND, U1.-, Part3.TX_5V
  VCC: Part1.VCC, Part2.5V
  N5: Part1.VM, U1.+
  N6: Part1.PWMA, Part2.D3
  N7: Part1.AIN2, Part2.D8
  N8: Part1.AIN1, Part2.D9
  N9: Part1.STBY, Part2.D10
  N10: Part1.BIN1, Part2.D11/MOSI
  N11: Part1.BIN2, Part2.D12/MISO
  N12: Part1.PWMB, Part2.D5
  N13: Part2.D1/TX, Part3.CTS_5V
  N14: Part2.D0/RX, Part3.VCC
  N15: Part2.3V3, Part3.RX_5V

notes:
  HM-05
