# Fritzing sketch rfduino (saved by Fritzing 0.9.3b)
breadboards: 1

parts:
  RFduino1 = RFduino
  Composant1 = Motor Driver 1A Dual TB6612FNG
  U2 = LIPO-110mAh [package=lipo-110]
  M2 = DC Motor
  M3 = DC Motor

nets:
  GND: RFduino1.gnd, Composant1.GND, U2.-
  VIN: RFduino1.vin, Composant1.VCC, Composant1.VM, U2.+
  N1: RFduino1.gpio0, Composant1.BIN2
  N2: RFduino1.gpio1, Composant1.PWMB
  N3: RFduino1.gpio2, Composant1.PWMA
  N4: RFduino1.gpio3, Composant1.AIN2
  N5: RFduino1.gpio4, Composant1.AIN1
  N6: RFduino1.gpio5, Composant1.STBY
  N7: RFduino1.gpio6, Composant1.BIN1
  N8: Composant1.B01, M2.pin_1
  N9: Composant1.B02, M2.pin_2
  N10: Composant1.A02, M3.pin_1
  N11: Composant1.A01, M3.pin_2

custom parts:
  RFduino: RFduino board
